// Logisim project OC.circ as structural Verilog: 20 circuits, main circuit main
module main (
);

  wire D_A, flag_1_cout_o, flag_1_equal_o, flag_1_larger_o, flag_1_zero_o, I_O, IO_e, IO_s, or_1_out,
       uc_1_ir_s, uc_1_out_20, uc_1_to_acc_e, uc_1_to_acc_s, uc_1_to_bus_1, uc_1_to_flags_s, uc_1_to_iar_e,
       uc_1_to_iar_s, uc_1_to_mar_s, uc_1_to_r0_e, uc_1_to_r0_s, uc_1_to_r1_e, uc_1_to_r1_s, uc_1_to_r2_e,
       uc_1_to_r2_s, uc_1_to_r3_e, uc_1_to_r3_s, uc_1_to_ram_e, uc_1_to_ram_s, uc_1_to_tmp_s, ula_1_a_maior,
       ula_1_cout, ula_1_igual, ula_1_zero;
  wire [2:0] uc_1_to_ula;
  wire [7:0] bus1_1_out_3, controlled_buffer_1_out, MAR_q, register_1_q, register_2_q, register_3_q,
       register_4_q, register_5_q, register_6_q, register_7_q, TMP_q, ula_1_result;

  ULA ula_1 (
    .A(controlled_buffer_1_out), .B(bus1_1_out_3), .Result(ula_1_result), .OP(uc_1_to_ula),
    .bus_1(uc_1_to_bus_1), .Cin(flag_1_cout_o), .Cout(ula_1_cout), .A_Maior(ula_1_a_maior),
    .Igual(ula_1_igual), .Zero(ula_1_zero));
  Register register_1 (.D(ula_1_result), .Q(register_1_q), .clk(uc_1_to_acc_s));  // open: en, clr
  Register TMP (.D(controlled_buffer_1_out), .Q(TMP_q), .clk(uc_1_to_tmp_s));  // open: en, clr
  assign controlled_buffer_1_out = uc_1_to_acc_e ? register_1_q : 8'bz;  // Controlled_Buffer controlled_buffer_1
  // Probe on controlled_buffer_1_out
  bus1 bus1_1 (.in_1(TMP_q), .out_3(bus1_1_out_3), .in_2(uc_1_to_bus_1));
  flag flag_1 (
    .Cout_I(ula_1_cout), .Larger_I(ula_1_a_maior), .Equal_I(ula_1_igual), .Zero_I(ula_1_zero),
    .Flag_s(uc_1_to_flags_s), .Cout_o(flag_1_cout_o), .Larger_o(flag_1_larger_o), .Equal_o(flag_1_equal_o),
    .Zero_o(flag_1_zero_o));
  assign controlled_buffer_1_out = uc_1_to_r0_e ? register_2_q : 8'bz;  // Controlled_Buffer controlled_buffer_2
  Register register_2 (.D(controlled_buffer_1_out), .Q(register_2_q), .clk(uc_1_to_r0_s));  // open: en, clr
  Register register_3 (.D(controlled_buffer_1_out), .Q(register_3_q), .clk(uc_1_to_iar_s));  // open: en, clr
  assign controlled_buffer_1_out = uc_1_to_iar_e ? register_3_q : 8'bz;  // Controlled_Buffer controlled_buffer_3
  assign controlled_buffer_1_out = uc_1_to_r1_e ? register_4_q : 8'bz;  // Controlled_Buffer controlled_buffer_4
  Register register_4 (.D(controlled_buffer_1_out), .Q(register_4_q), .clk(uc_1_to_r1_s));  // open: en, clr
  UC uc_1 (
    .to_ULA(uc_1_to_ula), .from_Carry_Out(flag_1_cout_o), .from_Larger(flag_1_larger_o),
    .from_Equal(flag_1_equal_o), .from_Zero(flag_1_zero_o), .to_Flags_s(uc_1_to_flags_s),
    .to_bus_1(uc_1_to_bus_1), .to_TMP_s(uc_1_to_tmp_s), .to_R0_s(uc_1_to_r0_s), .to_R0_e(uc_1_to_r0_e),
    .to_R1_s(uc_1_to_r1_s), .to_R1_e(uc_1_to_r1_e), .to_R2_s(uc_1_to_r2_s), .to_R2_e(uc_1_to_r2_e),
    .to_R3_s(uc_1_to_r3_s), .to_R3_e(uc_1_to_r3_e), .to_MAR_s(uc_1_to_mar_s), .to_ACC_s(uc_1_to_acc_s),
    .to_ACC_e(uc_1_to_acc_e), .to_IAR_s(uc_1_to_iar_s), .to_IAR_e(uc_1_to_iar_e), .from_IR(register_6_q),
    .IR_s(uc_1_ir_s), .Input_Output(I_O), .Data_Address(D_A), .to_IO_e(IO_e), .to_IO_s(IO_s),
    .to_RAM_s(uc_1_to_ram_s), .to_RAM_e(uc_1_to_ram_e), .out_20(uc_1_out_20));
  LED led_1 (.in(uc_1_out_20));
  assign controlled_buffer_1_out = uc_1_to_r2_e ? register_5_q : 8'bz;  // Controlled_Buffer controlled_buffer_5
  Register register_5 (.D(controlled_buffer_1_out), .Q(register_5_q), .clk(uc_1_to_r2_s));  // open: en, clr
  Register register_6 (.D(controlled_buffer_1_out), .Q(register_6_q), .clk(uc_1_ir_s));  // open: en, clr
  assign controlled_buffer_1_out = uc_1_to_r3_e ? register_7_q : 8'bz;  // Controlled_Buffer controlled_buffer_6
  Register register_7 (.D(controlled_buffer_1_out), .Q(register_7_q), .clk(uc_1_to_r3_s));  // open: en, clr
  Register MAR (.D(controlled_buffer_1_out), .Q(MAR_q), .clk(uc_1_to_mar_s));  // open: en, clr
  or or_1 (or_1_out, uc_1_to_ram_s, uc_1_to_ram_e);
  RAM #(.databus("bidir")) ram_1 (
    .addr(MAR_q), .we(uc_1_to_ram_s), .oe(uc_1_to_ram_e), .clk(or_1_out), .data(controlled_buffer_1_out));
  // Probe on controlled_buffer_1_out

  // Notes on the sheet:
  //   ULA
  //   ACC
  //   bus1
  //   000 | soma
  //   001 | S_Right
  //   010 | S_Left
  //   011 | Not
  //   100 | And
  //   101 | Or
  //   110 | Xor
  //   R0
  //   IAR
  //   UC
  //   R1
  //   R2
  //   IR
  //   WE = Write Enble
  //   OE = Output Enable
  //   Clock
  //   R3
endmodule

module somador1bit (
  input  Cin,
  input  A,
  input  B,
  output S,
  output Cout
);

  wire and_1_out, and_2_out, xor_1_out;

  and and_1 (and_1_out, A, B);
  xor xor_1 (xor_1_out, A, B);
  or or_1 (Cout, and_1_out, and_2_out);
  and and_2 (and_2_out, xor_1_out, Cin);
  xor xor_2 (S, Cin, xor_1_out);
endmodule

module somador8bits (
  input  [7:0] A,
  input  in_2,
  input  [7:0] B,
  output out_4,
  output [7:0] S
);

  wire somador1bit_1_cout, somador1bit_3_cout, somador1bit_4_cout, somador1bit_5_cout, somador1bit_6_cout,
       somador1bit_7_cout;

  somador1bit somador1bit_1 (.A(A[0]), .B(B[0]), .Cin(in_2), .Cout(somador1bit_1_cout), .S(S[0]));
  somador1bit somador1bit_2 (.A(A[1]), .B(B[1]), .Cin(somador1bit_1_cout), .Cout(B[2]), .S(S[1]));
  somador1bit somador1bit_3 (.A(A[2]), .B(B[2]), .Cin(B[2]), .Cout(somador1bit_3_cout), .S(S[2]));
  somador1bit somador1bit_4 (.A(A[3]), .B(B[3]), .Cin(somador1bit_3_cout), .Cout(somador1bit_4_cout), .S(S[3]));
  somador1bit somador1bit_5 (.A(A[4]), .B(B[4]), .Cin(somador1bit_4_cout), .Cout(somador1bit_5_cout), .S(S[4]));
  somador1bit somador1bit_6 (.A(A[5]), .B(B[5]), .Cin(somador1bit_5_cout), .Cout(somador1bit_6_cout), .S(S[5]));
  somador1bit somador1bit_7 (.A(A[6]), .B(B[6]), .Cin(somador1bit_6_cout), .Cout(somador1bit_7_cout), .S(S[6]));
  somador1bit somador1bit_8 (.A(A[7]), .B(B[7]), .Cin(somador1bit_7_cout), .Cout(out_4), .S(S[7]));
endmodule

module Memoria1Bit (
  input  I,
  input  S,
  output Q
);

  wire nand_1_out, nand_2_out, nand_4_out;

  nand nand_1 (nand_1_out, I, S);
  nand nand_2 (nand_2_out, nand_1_out, S);
  nand nand_3 (Q, nand_1_out, nand_4_out);
  nand nand_4 (nand_4_out, Q, nand_2_out);

  // Notes on the sheet:
  //   Input | Set | Output
  //   0   |  0  |  x
  //   1   |  0  |  x
  //   0   |  1  |  0
  //   1   |  1  |  1
  //   (armazenado)
  //   (armazenado)
endmodule

module Memoria8Bits (
  input  in_1,
  input  [7:0] in_2,
  output [7:0] out_3
);

  Memoria1Bit memoria1bit_1 (.S(in_1), .I(in_2[0]), .Q(out_3[0]));
  Memoria1Bit memoria1bit_2 (.S(in_1), .I(in_2[1]), .Q(out_3[1]));
  Memoria1Bit memoria1bit_3 (.S(in_1), .I(in_2[2]), .Q(out_3[2]));
  Memoria1Bit memoria1bit_4 (.S(in_1), .I(in_2[3]), .Q(out_3[3]));
  Memoria1Bit memoria1bit_5 (.S(in_1), .I(in_2[4]), .Q(out_3[4]));
  Memoria1Bit memoria1bit_6 (.S(in_1), .I(in_2[5]), .Q(out_3[5]));
  Memoria1Bit memoria1bit_7 (.S(in_1), .I(in_2[6]), .Q(out_3[6]));
  Memoria1Bit memoria1bit_8 (.S(in_1), .I(in_2[7]), .Q(out_3[7]));
endmodule

module Registrador (
  input  S,
  input  [7:0] I,
  input  E,
  output [7:0] O
);

  wire [7:0] memoria8bits_1_p3;

  // Memoria8Bits memoria8bits_1: pin names not known; wires that end beside it: I, S, memoria8bits_1_p3
  and and_1 (O[0], memoria8bits_1_p3[0], E);
  and and_2 (O[1], memoria8bits_1_p3[1], E);
  and and_3 (O[2], memoria8bits_1_p3[2], E);
  and and_4 (O[3], memoria8bits_1_p3[3], E);
  and and_5 (O[4], memoria8bits_1_p3[4], E);
  and and_6 (O[5], memoria8bits_1_p3[5], E);
  and and_7 (O[6], memoria8bits_1_p3[6], E);
  and and_8 (O[7], memoria8bits_1_p3[7], E);
endmodule

module Memoria1byte (
  input  Set,
  input  [7:0] Inp,
  output out_3,
  output out_4,
  output out_5,
  output out_6,
  output out_7,
  output out_8,
  output out_9,
  output out_10
);

  Memoria1Bit memoria1bit_1 (.S(Set), .I(Inp[0]), .Q(out_3));
  Memoria1Bit memoria1bit_2 (.S(Set), .I(Inp[1]), .Q(out_4));
  Memoria1Bit memoria1bit_3 (.S(Set), .I(Inp[2]), .Q(out_5));
  Memoria1Bit memoria1bit_4 (.S(Set), .I(Inp[3]), .Q(out_6));
  Memoria1Bit memoria1bit_5 (.S(Set), .I(Inp[4]), .Q(out_7));
  Memoria1Bit memoria1bit_6 (.S(Set), .I(Inp[5]), .Q(out_8));
  Memoria1Bit memoria1bit_7 (.S(Set), .I(Inp[6]), .Q(out_9));
  Memoria1Bit memoria1bit_8 (.S(Set), .I(Inp[7]), .Q(out_10));
endmodule

module Controll_buffer (
  input  in_1,
  input  in_2,
  input  in_3,
  input  in_4,
  input  in_5,
  input  [7:0] in_6,
  input  [2:0] in_7,
  output [7:0] out_8
);

  wire undriven, undriven_2, undriven_3;
  wire [7:0] controlled_buffer_1_out, MAR_q, ram_1_data, register_1_q, register_2_q;

  Shifter shifter_1 (.in(in_6), .\dist (in_7), .out(out_8));
  Register register_1 (.D(controlled_buffer_1_out), .Q(register_1_q), .clk(in_4));  // open: en, clr
  assign controlled_buffer_1_out = in_5 ? register_1_q : 8'bz;  // Controlled_Buffer controlled_buffer_1
  Register register_2 (.D(controlled_buffer_1_out), .Q(register_2_q), .clk(in_2));  // open: en, clr
  assign controlled_buffer_1_out = in_3 ? register_2_q : 8'bz;  // Controlled_Buffer controlled_buffer_2
  Register MAR (.D(controlled_buffer_1_out), .Q(MAR_q), .clk(in_1));  // open: en, clr
  RAM #(.databus("bidir")) ram_1 (.addr(MAR_q), .we(undriven), .oe(undriven_2), .clk(undriven_3), .data(ram_1_data));
endmodule

module MEM_RAM (
  input  [7:0] Dado,
  input  in_2,
  input  [7:0] Endereco,
  input  in_4,
  input  in_5,
  output [7:0] out_6
);

  wire and_1_out, and_2_out, and_3_out, and_4_out, and_5_out, and_6_out, and_7_out, and_8_out, and_9_out,
       decoder_1_out0, decoder_1_out1, decoder_1_out2, decoder_2_out0, undriven_3, undriven_4, undriven_5,
       undriven_6, undriven_7, undriven_8;
  wire [7:0] controlled_buffer_7_out, controlled_buffer_8_out, register_1_q, register_2_q, register_3_q,
       register_4_q, register_5_q, register_6_q, register_7_q, undriven, undriven_2;

  Decoder #(.select(4)) decoder_1 (
    .out0(decoder_1_out0), .out1(decoder_1_out1), .out2(decoder_1_out2), .sel(Endereco[3:0]));  // open: out3, out4, out5, out6, out7, out8, out9, out10, out11, out12, out13, out14, out15, en
  Decoder #(.select(4)) decoder_2 (
    .out0(decoder_2_out0), .sel(Endereco[7:4]));  // open: out1, out2, out3, out4, out5, out6, out7, out8, out9, out10, out11, out12, out13, out14, out15, en
  Register register_1 (.D(Dado), .Q(register_1_q), .clk(in_2));  // open: en, clr
  and and_1 (and_1_out, decoder_1_out0, decoder_2_out0);
  Register register_2 (.D(undriven), .Q(register_2_q), .clk(in_4));  // open: en, clr
  and and_2 (and_2_out, undriven_4, decoder_2_out0);
  Register register_3 (.D(undriven_2), .Q(register_3_q), .clk(in_5));  // open: en, clr
  and and_3 (and_3_out, undriven_3, decoder_2_out0);
  assign register_2_q = and_1_out ? register_1_q : 8'bz;  // Controlled_Buffer controlled_buffer_1
  assign register_3_q = and_2_out ? register_2_q : 8'bz;  // Controlled_Buffer controlled_buffer_2
  assign out_6 = and_3_out ? register_3_q : 8'bz;  // Controlled_Buffer controlled_buffer_3
  Register register_4 (.D(Dado), .Q(register_4_q));  // open: en, clk, clr
  and and_4 (and_4_out, decoder_1_out1, decoder_2_out0);
  Register register_5 (.D(undriven), .Q(register_5_q));  // open: en, clk, clr
  and and_5 (and_5_out, undriven_5, decoder_2_out0);
  Register register_6 (.D(undriven_2), .Q(register_6_q));  // open: en, clk, clr
  and and_6 (and_6_out, undriven_6, decoder_2_out0);
  assign register_5_q = and_4_out ? register_4_q : 8'bz;  // Controlled_Buffer controlled_buffer_4
  assign register_6_q = and_5_out ? register_5_q : 8'bz;  // Controlled_Buffer controlled_buffer_5
  assign out_6 = and_6_out ? register_6_q : 8'bz;  // Controlled_Buffer controlled_buffer_6
  and and_7 (and_7_out, decoder_1_out2, decoder_2_out0);
  and and_8 (and_8_out, undriven_7, decoder_2_out0);
  and and_9 (and_9_out, undriven_8, decoder_2_out0);
  Register register_7 (.D(Dado), .Q(register_7_q));  // open: en, clk, clr
  assign controlled_buffer_7_out = and_7_out ? register_7_q : 8'bz;  // Controlled_Buffer controlled_buffer_7
  Register register_8 (.D(undriven), .Q(controlled_buffer_7_out));  // open: en, clk, clr
  assign controlled_buffer_8_out = and_8_out ? controlled_buffer_7_out : 8'bz;  // Controlled_Buffer controlled_buffer_8
  Register register_9 (.D(undriven_2), .Q(controlled_buffer_8_out));  // open: en, clk, clr
  assign out_6 = and_9_out ? controlled_buffer_8_out : 8'bz;  // Controlled_Buffer controlled_buffer_9
endmodule

module ULA (
  input  [2:0] OP,
  input  [7:0] A,
  input  [7:0] B,
  input  bus_1,
  input  Cin,
  output Cout,
  output [7:0] Result,
  output A_Maior,
  output Igual,
  output Zero
);

  wire adder_1_cout, and_2_out, or_2_out, s_left_1_cout, s_right_1_cout;
  wire [7:0] adder_1_out, and_1_out, not_1_out, or_1_out, s_left_1_out_2, s_right_1_out_3, xor_1_out;

  Adder adder_1 (.a(A), .b(B), .out(adder_1_out), .cin(and_2_out), .cout(adder_1_cout));
  S_Right s_right_1 (.in_1(A), .Cout(s_right_1_cout), .out_3(s_right_1_out_3));
  S_Left s_left_1 (.in_1(A), .out_2(s_left_1_out_2), .Cout(s_left_1_cout));
  assign not_1_out = ~A;  // NOT_Gate not_1, 8 bits wide
  assign and_1_out = A & B;  // AND_Gate and_1, 8 bits wide
  assign or_1_out = A | B;  // OR_Gate or_1, 8 bits wide
  assign xor_1_out = A ^ B;  // XOR_Gate xor_1, 8 bits wide
  Comparator comparator_1 (.a(A), .b(B), .gt(A_Maior), .eq(Igual));  // open: lt
  Multiplexer #(.select(3), .width(8)) multiplexer_1 (
    .in0(adder_1_out), .in1(s_right_1_out_3), .in2(s_left_1_out_2), .in3(not_1_out), .in4(and_1_out),
    .in5(or_1_out), .in6(xor_1_out), .in7(A), .out(Result), .sel(OP));
  and and_2 (and_2_out, ~bus_1, Cin);  // AND_Gate
  Multiplexer #(.select(3)) multiplexer_2 (
    .in0(adder_1_cout), .in1(s_right_1_cout), .in2(s_left_1_cout), .in3(1'b0), .in4(1'b0), .in5(1'b0),
    .in6(1'b0), .in7(1'b0), .out(Cout), .sel(OP));
  or or_2 (or_2_out, Result[0], Result[1], Result[2], Result[3], Result[4], Result[5], Result[6], Result[7]);
  not not_2 (Zero, or_2_out);
endmodule

module S_Left (
  input  [7:0] in_1,
  output [7:0] out_2,
  output Cout
);


  assign Cout = in_1[7];
  assign out_2 = {in_1[6:0], 1'b0};
endmodule

module S_Right (
  input  [7:0] in_1,
  output Cout,
  output [7:0] out_3
);


  assign Cout = in_1[0];
  assign out_3 = {{2{in_1[7]}}, in_1[6:1]};
endmodule

module bus1 (
  input  [7:0] in_1,
  input  in_2,
  output [7:0] out_3
);

  Multiplexer #(.width(8)) multiplexer_1 (.in0(in_1), .in1(8'h1), .out(out_3), .sel(in_2));
endmodule

module clocker (
  output clk_s,
  output out_2,
  output clk_e
);

  wire clk_d_out;

  Clock #(.highDuration(2), .lowDuration(2)) clk (.out(out_2));
  Clock #(.highDuration(2), .lowDuration(2), .phaseOffset(3)) clk_d (.out(clk_d_out));
  and and_1 (clk_s, out_2, clk_d_out);
  or or_1 (clk_e, out_2, clk_d_out);
endmodule

module Stepper (
  input  in_1,
  output init_cycle,
  output out_3,
  output out_4,
  output out_5,
  output out_6,
  output out_7,
  output out_8
);

  wire decoder_1_out7;
  wire [2:0] counter_1_q;

  Counter #(.max('h7), .width(3)) counter_1 (
    .load(1'b0), .Q(counter_1_q), .up(1'b1), .clk(in_1), .clr(decoder_1_out7));  // open: D, count, carry
  Decoder #(.enable("false"), .select(3)) decoder_1 (
    .out0(init_cycle), .out1(out_3), .out2(out_4), .out3(out_5), .out4(out_6), .out5(out_7), .out6(out_8),
    .out7(decoder_1_out7), .sel(counter_1_q));
endmodule

module UC (
  input  from_Carry_Out,
  input  from_Larger,
  input  from_Equal,
  input  from_Zero,
  input  [7:0] from_IR,
  output to_TMP_s,
  output to_R0_s,
  output to_R0_e,
  output to_R1_s,
  output to_R1_e,
  output to_R2_s,
  output to_R2_e,
  output to_R3_s,
  output to_R3_e,
  output to_MAR_s,
  output to_bus_1,
  output to_RAM_s,
  output [2:0] to_ULA,
  output to_RAM_e,
  output out_20,
  output to_Flags_s,
  output to_ACC_s,
  output to_ACC_e,
  output to_IAR_s,
  output to_IAR_e,
  output IR_s,
  output Input_Output,
  output Data_Address,
  output to_IO_e,
  output to_IO_s
);

  wire A_out, and_8_out, and_9_out, and_10_out, and_11_out, and_12_out, and_13_out, and_14_out, and_15_out,
       and_16_out, and_17_out, and_18_out, and_19_out, and_20_out, and_21_out, and_22_out, and_23_out,
       and_24_out, and_25_out, and_26_out, and_27_out, C_out, clk_e, clk_s, Clock_out_2, decoder_3x8_1_out_5,
       decoder_3x8_1_out_6, decoder_3x8_1_out_7, decoder_3x8_1_out_8, decoder_3x8_1_out_9,
       decoder_3x8_1_out_10, decoder_3x8_1_out_11, decoder_3x8_1_out_12, decoder_3x8_1_out_13, E_out,
       not_1_out, not_2_out, or_1_out, or_3_out, or_4_out, or_5_out, or_6_out, or_7_out, or_8_out, or_9_out,
       or_10_out, or_11_out, or_12_out, s1, s2, s3, s4, s5, s6, Z_out;

  and and_1 (to_IAR_e, or_3_out, clk_e);
  and and_2 (to_RAM_e, or_4_out, clk_e);
  and and_3 (to_ACC_e, or_5_out, clk_e);
  and and_4 (to_IO_e, and_24_out, clk_e);
  clocker Clock (.clk_s(clk_s), .out_2(Clock_out_2), .clk_e(clk_e));
  decoder_2 decoder_2_1 (
    .out_8(to_R0_e), .out_9(to_R1_e), .out_10(to_R2_e), .out_11(to_R3_e), .e(clk_e), .rb(or_1_out),
    .ra(or_6_out), .in_4(from_IR[0]), .in_5(from_IR[1]), .in_6(from_IR[2]), .in_7(from_IR[3]));
  or or_1 (or_1_out, and_8_out, and_20_out, and_12_out, and_16_out);
  or or_2 (to_bus_1, s1, and_15_out, and_14_out, and_11_out);
  or or_3 (or_3_out, s1, and_11_out, and_13_out, and_14_out);
  or or_4 (or_4_out, s2, and_27_out, and_22_out, and_21_out, and_19_out);
  or or_5 (or_5_out, s3, and_23_out, and_26_out, and_25_out);
  or or_6 (or_6_out, and_10_out, and_9_out, and_18_out);
  and and_5 (to_ULA[0], s5, from_IR[7], from_IR[4]);
  and and_6 (to_ULA[1], s5, from_IR[7], from_IR[5]);
  and and_7 (to_ULA[2], s5, from_IR[7], from_IR[6]);
  Stepper Step (
    .in_1(Clock_out_2), .out_3(s1), .out_4(s2), .out_5(s3), .out_6(s4), .out_7(s5), .out_8(s6),
    .init_cycle(out_20));
  decoder_3x8 decoder_3x8_1 (
    .out_5(decoder_3x8_1_out_5), .in_1(from_IR[7]), .in_2(from_IR[6]), .in_3(from_IR[5]), .in_4(from_IR[4]),
    .out_6(decoder_3x8_1_out_6), .out_7(decoder_3x8_1_out_7), .out_8(decoder_3x8_1_out_8),
    .out_9(decoder_3x8_1_out_9), .out_10(decoder_3x8_1_out_10), .out_11(decoder_3x8_1_out_11),
    .out_12(decoder_3x8_1_out_12), .out_13(decoder_3x8_1_out_13));
  and and_8 (and_8_out, s4, decoder_3x8_1_out_5);
  and and_9 (and_9_out, s4, decoder_3x8_1_out_6);
  and and_10 (and_10_out, s4, decoder_3x8_1_out_7);
  and and_11 (and_11_out, s4, decoder_3x8_1_out_8);
  and and_12 (and_12_out, s4, decoder_3x8_1_out_9);
  and and_13 (and_13_out, s4, decoder_3x8_1_out_10);
  and and_14 (and_14_out, s4, decoder_3x8_1_out_11);
  and and_15 (and_15_out, s4, decoder_3x8_1_out_12);
  and and_16 (and_16_out, s4, decoder_3x8_1_out_13, from_IR[3]);
  and and_17 (and_17_out, from_IR[4], from_IR[5], from_IR[6]);
  not not_1 (not_1_out, and_17_out);
  and C (C_out, from_IR[3], from_Carry_Out);
  and A (A_out, from_IR[2], from_Larger);
  and E (E_out, from_IR[1], from_Equal);
  and Z (Z_out, from_IR[0], from_Zero);
  not not_2 (not_2_out, from_IR[3]);
  and and_18 (and_18_out, s5, decoder_3x8_1_out_5);
  and and_19 (and_19_out, s5, decoder_3x8_1_out_6);
  and and_20 (and_20_out, s5, decoder_3x8_1_out_7);
  and and_21 (and_21_out, s5, decoder_3x8_1_out_8);
  and and_22 (and_22_out, s5, decoder_3x8_1_out_10);
  and and_23 (and_23_out, s5, decoder_3x8_1_out_11);
  and and_24 (and_24_out, s5, decoder_3x8_1_out_13, not_2_out);
  or or_7 (or_7_out, C_out, A_out, E_out, Z_out);
  and and_25 (and_25_out, s6, decoder_3x8_1_out_5, not_1_out);
  and and_26 (and_26_out, s6, decoder_3x8_1_out_8);
  and and_27 (and_27_out, s6, decoder_3x8_1_out_11, or_7_out);
  or or_8 (or_8_out, s1, and_11_out, and_14_out, and_9_out, and_10_out, and_13_out);
  or or_9 (or_9_out, s3, and_12_out, and_22_out, and_23_out, and_26_out, and_27_out);
  or or_10 (or_10_out, s1, and_11_out, and_14_out, and_18_out);
  or or_11 (or_11_out, and_19_out, and_25_out, and_21_out, and_24_out);
  or or_12 (or_12_out, and_15_out, and_18_out);
  decoder_2x4 decoder_2x4_1 (
    .in_1(or_11_out), .in_2(clk_s), .in_3(from_IR[1]), .in_4(from_IR[0]), .out_5(to_R0_s), .out_6(to_R1_s),
    .out_7(to_R2_s), .out_8(to_R3_s));
  and and_28 (IR_s, clk_s, s2);
  and and_29 (to_MAR_s, clk_s, or_8_out);
  and and_30 (to_IAR_s, clk_s, or_9_out);
  and and_31 (to_ACC_s, clk_s, or_10_out);
  and and_32 (to_RAM_s, clk_s, and_20_out);
  and and_33 (to_TMP_s, clk_s, and_8_out);
  and and_34 (to_Flags_s, clk_s, or_12_out);
  and and_35 (to_IO_s, clk_s, and_14_out);

  assign Data_Address = from_IR[2];
  assign Input_Output = from_IR[3];

  // Other names for the same wires on the sheet: init = out_20
endmodule

module decoder_2 (
  input  e,
  input  rb,
  input  ra,
  input  in_4,
  input  in_5,
  input  in_6,
  input  in_7,
  output out_8,
  output out_9,
  output out_10,
  output out_11
);

  wire and_1_out, and_2_out, and_3_out, and_4_out, and_5_out, and_6_out, and_7_out, and_8_out,
       decoder_1_out0, decoder_1_out1, decoder_1_out2, decoder_1_out3, decoder_2_out0, decoder_2_out1,
       decoder_2_out2, decoder_2_out3;

  or or_1 (out_8, and_1_out, and_5_out);
  or or_2 (out_9, and_2_out, and_6_out);
  or or_3 (out_10, and_3_out, and_7_out);
  or or_4 (out_11, and_4_out, and_8_out);
  and and_1 (and_1_out, e, rb, decoder_1_out0);
  and and_2 (and_2_out, e, rb, decoder_1_out1);
  and and_3 (and_3_out, e, rb, decoder_1_out2);
  and and_4 (and_4_out, e, rb, decoder_1_out3);
  and and_5 (and_5_out, e, decoder_2_out0, ra);
  and and_6 (and_6_out, e, decoder_2_out1, ra);
  and and_7 (and_7_out, e, decoder_2_out2, ra);
  and and_8 (and_8_out, e, decoder_2_out3, ra);
  Decoder #(.enable("false"), .select(2)) decoder_1 (
    .out0(decoder_1_out0), .out1(decoder_1_out1), .out2(decoder_1_out2), .out3(decoder_1_out3),
    .sel({in_5, in_4}));
  Decoder #(.enable("false"), .select(2)) decoder_2 (
    .out0(decoder_2_out0), .out1(decoder_2_out1), .out2(decoder_2_out2), .out3(decoder_2_out3),
    .sel({in_7, in_6}));
endmodule

module decoder_3x8 (
  input  in_1,
  input  in_2,
  input  in_3,
  input  in_4,
  output out_5,
  output out_6,
  output out_7,
  output out_8,
  output out_9,
  output out_10,
  output out_11,
  output out_12,
  output out_13
);

  wire decoder_1_out0, decoder_1_out1, decoder_1_out2, decoder_1_out3, decoder_1_out4, decoder_1_out5,
       decoder_1_out6, decoder_1_out7, not_1_out;

  not not_1 (not_1_out, in_1);
  Decoder #(.enable("false"), .select(3)) decoder_1 (
    .out0(decoder_1_out0), .out1(decoder_1_out1), .out2(decoder_1_out2), .out3(decoder_1_out3),
    .out4(decoder_1_out4), .out5(decoder_1_out5), .out6(decoder_1_out6), .out7(decoder_1_out7),
    .sel({in_2, in_3, in_4}));
  and and_1 (out_6, not_1_out, decoder_1_out0);
  and and_2 (out_7, not_1_out, decoder_1_out1);
  and and_3 (out_8, not_1_out, decoder_1_out2);
  and and_4 (out_9, not_1_out, decoder_1_out3);
  and and_5 (out_10, not_1_out, decoder_1_out4);
  and and_6 (out_11, not_1_out, decoder_1_out5);
  and and_7 (out_12, not_1_out, decoder_1_out6);
  and and_8 (out_13, not_1_out, decoder_1_out7);

  assign out_5 = in_1;
endmodule

module decoder_2x4 (
  input  in_1,
  input  in_2,
  input  in_3,
  input  in_4,
  output out_5,
  output out_6,
  output out_7,
  output out_8
);

  wire decoder_1_out0, decoder_1_out1, decoder_1_out2, decoder_1_out3;

  Decoder #(.enable("false"), .select(2)) decoder_1 (
    .out0(decoder_1_out0), .out1(decoder_1_out1), .out2(decoder_1_out2), .out3(decoder_1_out3),
    .sel({in_3, in_4}));
  and and_1 (out_5, decoder_1_out0, in_1, in_2);
  and and_2 (out_6, decoder_1_out1, in_1, in_2);
  and and_3 (out_7, decoder_1_out2, in_1, in_2);
  and and_4 (out_8, decoder_1_out3, in_1, in_2);
endmodule

module flag (
  input  Cout_I,
  input  Larger_I,
  input  Equal_I,
  input  Flag_s,
  input  Zero_I,
  output Cout_o,
  output Larger_o,
  output Equal_o,
  output Zero_o
);

  Register #(.width(4)) register_1 (
    .D({Zero_I, Equal_I, Larger_I, Cout_I}), .Q({Zero_o, Equal_o, Larger_o, Cout_o}), .clk(Flag_s));  // open: en, clr
endmodule
