// Logisim project Somador.circ as structural Verilog: 3 circuits, main circuit somador8bits
module main (
  input  in_1,
  input  [7:0] in_2,
  input  [7:0] in_3,
  output [7:0] out_4,
  output out_5
);

  somador8bits somador8bits_1 (.B(in_3), .A(in_2), .in_2(in_1), .S(out_4), .out_4(out_5));
endmodule

module somador1bit (
  input  Cin,
  input  A,
  input  B,
  output S,
  output Cout
);

  wire and_1_out, and_2_out, xor_1_out;

  and and_1 (and_1_out, A, B);
  xor xor_1 (xor_1_out, A, B);
  or or_1 (Cout, and_1_out, and_2_out);
  and and_2 (and_2_out, xor_1_out, Cin);
  xor xor_2 (S, Cin, xor_1_out);
endmodule

module somador8bits (
  input  [7:0] A,
  input  in_2,
  input  [7:0] B,
  output out_4,
  output [7:0] S
);

  wire somador1bit_1_cout, somador1bit_3_cout, somador1bit_4_cout, somador1bit_5_cout, somador1bit_6_cout,
       somador1bit_7_cout;

  somador1bit somador1bit_1 (.A(A[0]), .B(B[0]), .Cin(in_2), .Cout(somador1bit_1_cout), .S(S[0]));
  somador1bit somador1bit_2 (.A(A[1]), .B(B[1]), .Cin(somador1bit_1_cout), .Cout(B[2]), .S(S[1]));
  somador1bit somador1bit_3 (.A(A[2]), .B(B[2]), .Cin(B[2]), .Cout(somador1bit_3_cout), .S(S[2]));
  somador1bit somador1bit_4 (.A(A[3]), .B(B[3]), .Cin(somador1bit_3_cout), .Cout(somador1bit_4_cout), .S(S[3]));
  somador1bit somador1bit_5 (.A(A[4]), .B(B[4]), .Cin(somador1bit_4_cout), .Cout(somador1bit_5_cout), .S(S[4]));
  somador1bit somador1bit_6 (.A(A[5]), .B(B[5]), .Cin(somador1bit_5_cout), .Cout(somador1bit_6_cout), .S(S[5]));
  somador1bit somador1bit_7 (.A(A[6]), .B(B[6]), .Cin(somador1bit_6_cout), .Cout(somador1bit_7_cout), .S(S[6]));
  somador1bit somador1bit_8 (.A(A[7]), .B(B[7]), .Cin(somador1bit_7_cout), .Cout(out_4), .S(S[7]));
endmodule
